// Logisim project Forwarding.circ as structural Verilog: 1 circuit, main circuit main
module main (
);

  wire and_1_out, and_2_out, and_3_out, comparator_1_eq, comparator_2_eq, comparator_3_eq, comparator_4_eq,
       comparator_5_eq, comparator_6_eq, comparator_7_eq, comparator_8_eq, comparator_9_eq, comparator_10_eq,
       comparator_11_eq, comparator_12_eq, comparator_13_eq, comparator_14_eq, comparator_15_eq,
       comparator_16_eq, comparator_17_eq, not_1_out, not_2_out, not_3_out, not_4_out, or_1_out, or_2_out,
       or_3_out;
  wire [3:0] multiplexer_1_out, multiplexer_2_out, multiplexer_3_out;
  wire [31:0] A_q, B_q;

  Register #(.width(32)) A (.Q(A_q));  // open: D, en, clk, clr
  Register #(.width(32)) B (.Q(B_q));  // open: D, en, clk, clr
  Comparator #(.width(5)) comparator_1 (.a(5'b01111), .b(A_q[31:27]), .eq(comparator_1_eq));  // open: gt, lt
  Comparator #(.width(5)) comparator_2 (.a(5'b10010), .b(A_q[31:27]), .eq(comparator_2_eq));  // open: gt, lt
  Comparator #(.width(5)) comparator_3 (.a(5'b10000), .b(A_q[31:27]), .eq(comparator_3_eq));  // open: gt, lt
  Comparator #(.width(5)) comparator_4 (.a(5'b10001), .b(A_q[31:27]), .eq(comparator_4_eq));  // open: gt, lt
  Comparator #(.width(5)) comparator_5 (.a(5'b01101), .b(A_q[31:27]), .eq(comparator_5_eq));  // open: gt, lt
  Comparator #(.width(5)) comparator_6 (.a(5'b10011), .b(A_q[31:27]), .eq(comparator_6_eq));  // open: gt, lt
  Comparator #(.width(5)) comparator_7 (.a(5'b10100), .b(A_q[31:27]), .eq(comparator_7_eq));  // open: gt, lt
  Comparator #(.width(5)) comparator_8 (.a(5'b01101), .b(B_q[31:27]), .eq(comparator_8_eq));  // open: gt, lt
  Comparator #(.width(5)) comparator_9 (.a(5'b00101), .b(B_q[31:27]), .eq(comparator_9_eq));  // open: gt, lt
  Comparator #(.width(5)) comparator_10 (.a(5'b01111), .b(B_q[31:27]), .eq(comparator_10_eq));  // open: gt, lt
  Comparator #(.width(5)) comparator_11 (.a(5'b10000), .b(B_q[31:27]), .eq(comparator_11_eq));  // open: gt, lt
  Comparator #(.width(5)) comparator_12 (.a(5'b10001), .b(B_q[31:27]), .eq(comparator_12_eq));  // open: gt, lt
  Comparator #(.width(5)) comparator_13 (.a(5'b10010), .b(B_q[31:27]), .eq(comparator_13_eq));  // open: gt, lt
  Comparator #(.width(5)) comparator_14 (.a(5'b10100), .b(B_q[31:27]), .eq(comparator_14_eq));  // open: gt, lt
  Comparator #(.width(5)) comparator_15 (.a(5'b10011), .b(B_q[31:27]), .eq(comparator_15_eq));  // open: gt, lt
  not not_1 (not_1_out, comparator_1_eq);
  and and_1 (and_1_out, A_q[26], not_1_out);
  or or_1 (or_1_out, comparator_2_eq, comparator_3_eq, comparator_4_eq, comparator_5_eq, comparator_6_eq);
  not not_2 (not_2_out, or_1_out);
  Multiplexer #(.width(4)) multiplexer_1 (
    .in0(A_q[25:22]), .in1(4'b1111), .out(multiplexer_1_out), .sel(comparator_7_eq));  // open: en
  not not_3 (not_3_out, or_2_out);
  or or_2 (or_2_out, comparator_8_eq, comparator_9_eq, comparator_10_eq, comparator_11_eq, comparator_12_eq, comparator_13_eq, comparator_14_eq);
  Multiplexer #(.width(4)) multiplexer_2 (
    .in0(B_q[25:22]), .in1(4'b1111), .out(multiplexer_2_out), .sel(comparator_15_eq));  // open: en
  not not_4 (not_4_out, and_1_out);
  Multiplexer #(.width(4)) multiplexer_3 (
    .in0(A_q[17:14]), .in1(A_q[25:22]), .out(multiplexer_3_out), .sel(comparator_1_eq));  // open: en
  Comparator #(.width(4)) comparator_16 (
    .a(multiplexer_3_out), .b(multiplexer_2_out), .eq(comparator_16_eq));  // open: gt, lt
  Comparator #(.width(4)) comparator_17 (
    .a(multiplexer_1_out), .b(multiplexer_2_out), .eq(comparator_17_eq));  // open: gt, lt
  and and_2 (and_2_out, not_4_out, not_2_out, not_3_out, not_3_out);
  and and_3 (and_3_out, comparator_17_eq, not_2_out, not_3_out);
  or or_3 (or_3_out, and_2_out, and_3_out);
endmodule
