// Logisim project ForwardingIsABitch.circ as structural Verilog: 1 circuit, main circuit main
module main (
  input  [31:0] in_1,
  input  [31:0] in_2
);

  wire and_1_out, comparator_1_eq, comparator_2_eq, comparator_3_eq, comparator_4_eq, comparator_5_eq,
       comparator_6_eq, comparator_7_eq, comparator_8_eq, comparator_9_eq, comparator_10_eq,
       comparator_11_eq, comparator_12_eq, comparator_13_eq, comparator_14_eq, comparator_15_eq, not_1_out,
       or_1_out, or_2_out, or_3_out;
  wire [3:0] multiplexer_1_out, multiplexer_2_out;

  Comparator #(.width(5)) comparator_1 (.a(5'b10100), .b(in_1[31:27]), .eq(comparator_1_eq));  // open: gt, lt
  Comparator #(.width(5)) comparator_2 (.a(in_1[31:27]), .b(5'b01101), .eq(comparator_2_eq));  // open: gt, lt
  Comparator #(.width(5)) comparator_3 (.a(in_1[31:27]), .b(5'b10000), .eq(comparator_3_eq));  // open: gt, lt
  Comparator #(.width(5)) comparator_4 (.a(in_1[31:27]), .b(5'b01110), .eq(comparator_4_eq));  // open: gt, lt
  Comparator #(.width(5)) comparator_5 (.a(in_1[31:27]), .b(5'b01111), .eq(comparator_5_eq));  // open: gt, lt
  Comparator #(.width(5)) comparator_6 (.a(in_1[31:27]), .b(5'b10011), .eq(comparator_6_eq));  // open: gt, lt
  Comparator #(.width(5)) comparator_7 (.a(in_2[31:27]), .b(5'b10011), .eq(comparator_7_eq));  // open: gt, lt
  Comparator #(.width(5)) comparator_8 (.a(in_2[31:27]), .b(5'b01101), .eq(comparator_8_eq));  // open: gt, lt
  Comparator #(.width(5)) comparator_9 (.a(in_2[31:27]), .b(5'b00101), .eq(comparator_9_eq));  // open: gt, lt
  Comparator #(.width(5)) comparator_10 (.a(in_2[31:27]), .b(5'b10010), .eq(comparator_10_eq));  // open: gt, lt
  Comparator #(.width(5)) comparator_11 (.a(in_2[31:27]), .b(5'b10000), .eq(comparator_11_eq));  // open: gt, lt
  Comparator #(.width(5)) comparator_12 (.a(in_2[31:27]), .b(5'b01110), .eq(comparator_12_eq));  // open: gt, lt
  Comparator #(.width(5)) comparator_13 (.a(in_2[31:27]), .b(5'b01111), .eq(comparator_13_eq));  // open: gt, lt
  Comparator #(.width(5)) comparator_14 (.a(in_2[31:27]), .b(5'b10100), .eq(comparator_14_eq));  // open: gt, lt
  Multiplexer #(.width(4)) multiplexer_1 (
    .in0(in_1[21:18]), .in1(4'b1111), .out(multiplexer_1_out), .sel(comparator_1_eq));  // open: en
  Multiplexer #(.width(4)) multiplexer_2 (
    .in0(in_2[25:22]), .in1(4'b1111), .out(multiplexer_2_out), .sel(comparator_7_eq));  // open: en
  or or_1 (or_1_out, comparator_2_eq, comparator_3_eq, comparator_4_eq, comparator_5_eq, comparator_6_eq);
  or or_2 (or_2_out, comparator_8_eq, comparator_9_eq, comparator_10_eq, comparator_11_eq, comparator_12_eq, comparator_13_eq, comparator_14_eq);
  or or_3 (or_3_out, or_1_out, or_2_out);
  not not_1 (not_1_out, or_3_out);
  Comparator #(.width(4)) comparator_15 (
    .a(multiplexer_1_out), .b(multiplexer_2_out), .eq(comparator_15_eq));  // open: gt, lt
  and and_1 (and_1_out, not_1_out, comparator_15_eq);
endmodule
