// Logisim project Processor.circ as structural Verilog: 18 circuits, main circuit main
module main (
  input  [3:0] Register_Number,
  input  Reset,
  output [31:0] out_3
);

  wire Clock_out, isBeq, isBgt, isBranchTaken, isCall, isImmediate, isLd, isRet, isSt, isUbranch;
  wire [3:0] Address, aluSignals, undriven, undriven_2;
  wire [23:0] branchTarget, PC;
  wire [31:0] A, aluResult, B, bT, ldResult, op2, storeData;
  wire [31:8] undriven_3;

  Clock Clock (.out(Clock_out));
  // IF if_1: pin names not known; wires that end beside it: branchTarget, isBranchTaken, Clock_out, Reset
  MA ma_1 (.ldResult(ldResult), .op2(op2), .isLd(isLd), .isSt(isSt), .ALUResult(aluResult), .Clock(Clock_out));
  OF of_1 (
    .Instruction(out_3), .PC(PC), .isSt(isSt), .isImmx(isImmediate), .isRet(isRet), .writeData(storeData),
    .writeAddress(Address));  // open: branchTarget, A, B, op2, isWb, clock, displayAddress, displayOut, isCall, data, PinOP2, PinOP1
  EXU exu_1 (
    .isBeq(isBeq), .isUbranch(isUbranch), .isBgt(isBgt), .branchTargetIn(bT), .A(A), .aluSignals(aluSignals),
    .B(B), .Clock(Clock_out), .isBranchTaken(isBranchTaken), .branchTargetOut(branchTarget),
    .ALUResult(aluResult), .isRet(isRet));
  RW rw_1 (
    .Instruction(out_3), .ldResult(ldResult), .isLd(isLd), .ALUResult(aluResult), .isCall(isCall), .PC(PC),
    .Address(Address), .storeData(storeData));
  Hex_Digit_Display hex_digit_display_1 (.value(undriven_3[31:28]));  // open: dp
  Hex_Digit_Display hex_digit_display_2 (.value(undriven_3[23:20]));  // open: dp
  Hex_Digit_Display hex_digit_display_3 (.value(undriven_3[27:24]));  // open: dp
  Hex_Digit_Display hex_digit_display_4 (.value(undriven_3[15:12]));  // open: dp
  Hex_Digit_Display hex_digit_display_5 (.value(undriven_3[19:16]));  // open: dp
  CU cu_1 ();  // open: isWb, isUbranch, isImmediate, isLd, isSt, isBeq, isBgt, isCall, isRet, ALUSignals, Instruction
  Hex_Digit_Display hex_digit_display_6 (.value(undriven_2));  // open: dp
  Hex_Digit_Display hex_digit_display_7 (.value(undriven_3[11:8]));  // open: dp
  Hex_Digit_Display hex_digit_display_8 (.value(undriven));  // open: dp

  // Other names for the same wires on the sheet: Instruction[31:0] = out_3

  // Notes on the sheet:
  //   Note: The last instruction should be provided as "ffffffff" otherwise it will keep on interpreting "00000000", i.e. it will keep on doubling r0.
endmodule

module IF (
  input  [23:0] branchTarget,
  input  isBranchTaken,
  input  IFstageclock,
  input  reset,
  output [31:0] Instruction,
  output [23:0] PC
);

  wire and_1_out, multiplexer_1_out, not_1_out, not_2_out;

  not not_1 (not_1_out, IFstageclock);
  not not_2 (not_2_out, isBranchTaken);
  Multiplexer #(.enable("false")) multiplexer_1 (.in0(not_1_out), .in1(1'b1), .out(multiplexer_1_out), .sel(and_1_out));
  Counter #(.width(24), .max('hffffff)) counter_1 (
    .load(isBranchTaken), .D(branchTarget), .count(not_2_out), .Q(PC), .clk(multiplexer_1_out), .clr(reset));  // open: carry
  ROM #(.addrWidth(24), .dataWidth(32)) rom_1 (.addr(PC), .data(Instruction));  // open: sel
  and and_1 (and_1_out, Instruction[31], Instruction[30], Instruction[29], Instruction[28], Instruction[27], Instruction[26], Instruction[25], Instruction[24], Instruction[23], Instruction[22], Instruction[21], Instruction[20], Instruction[19], Instruction[18], Instruction[17], Instruction[16], Instruction[14], Instruction[13], Instruction[12], Instruction[11], Instruction[10], Instruction[9], Instruction[8], Instruction[7], Instruction[6], Instruction[5], Instruction[4], Instruction[3], Instruction[2], Instruction[1], Instruction[0], Instruction[15]);

  // Notes on the sheet:
  //   reset: pull=down
  //   IF Stage
  //   Counter for going to the next instruction
  //   Note: The last instruction should be provided as "ffffffff" otherwise it will keep on interpreting "00000000", i.e. it will keep on doubling r0.
  //   contents of rom_1 (hex, n*v repeats v):
  //   4c0006b8 4d000000 4d400000 4d800000 4cc00000 4c400001 11044000 11104000 28100000 88000011 4c800001
  //   28084000 8800000c 11488000 11548000 1914000 28180000 80000002 90000004 4cc0001 2c0c0002 80000007
  //   4880001 97fffff4 4440001 97ffffed 4000001 97ffffe9 90000000 ffffffff
  //   Used to stop instruction processing on encountering code "ffffffff".
endmodule

module OF (
  input  isRet,
  input  [23:0] PC,
  input  isImmx,
  input  [31:0] Instruction,
  input  PinOP2,
  input  PinOP1,
  input  isCall,
  input  [3:0] writeAddress,
  input  [31:0] writeData,
  input  isWb,
  input  clock,
  input  isSt,
  input  [3:0] displayAddress,
  input  [31:0] data,
  output [31:0] A,
  output [31:0] op2,
  output [31:0] B,
  output [31:0] displayOut,
  output [31:0] branchTarget
);

  wire and_1_out, or_1_out;
  wire [3:0] multiplexer_2_out, multiplexer_3_out;
  wire [31:0] A_t, adder_1_out, bit_extender_1_out, bit_extender_2_out, bit_extender_3_out,
       bit_extender_4_out, immx, op2_t, shifter_1_out;

  assign bit_extender_1_out = {{5{Instruction[26]}}, Instruction[26:0]};  // Bit_Extender bit_extender_1
  assign bit_extender_2_out = {{8{1'b0}}, PC};  // Bit_Extender bit_extender_2
  Multiplexer #(.width(32), .enable("false")) multiplexer_1 (
    .in0(adder_1_out), .in1(A_t), .out(branchTarget), .sel(isRet));
  Adder #(.width(32)) adder_1 (.a(bit_extender_1_out), .b(bit_extender_2_out), .out(adder_1_out));  // open: cin, cout
  assign bit_extender_3_out = {{16{Instruction[15]}}, Instruction[15:0]};  // Bit_Extender bit_extender_3
  assign bit_extender_4_out = {{16{1'b0}}, Instruction[15:0]};  // Bit_Extender bit_extender_4
  Shifter #(.width(32)) shifter_1 (.in(bit_extender_4_out), .\dist (5'b10000), .out(shifter_1_out));
  Multiplexer #(.width(4), .enable("false")) multiplexer_2 (
    .in0(Instruction[21:18]), .in1(4'b1111), .out(multiplexer_2_out), .sel(isRet));
  Multiplexer #(.width(4), .enable("false")) multiplexer_3 (
    .in0(Instruction[17:14]), .in1(Instruction[25:22]), .out(multiplexer_3_out), .sel(isSt));
  Multiplexer #(.select(2), .width(32), .enable("false")) multiplexer_4 (
    .in0(bit_extender_3_out), .in1(bit_extender_4_out), .in2(shifter_1_out), .out(immx),
    .sel(Instruction[17:16]));  // open: in3
  regFile regfile_1 (
    .writeData(writeData), .writeAddress(writeAddress), .clock(and_1_out), .readB(multiplexer_3_out),
    .outB(op2_t), .outA(A_t), .readA(multiplexer_2_out), .displayOut(displayOut), .displayRead(displayAddress));
  and and_1 (and_1_out, or_1_out, clock);
  or or_1 (or_1_out, isCall, isWb);
  Multiplexer #(.width(32), .enable("false")) multiplexer_5 (.in0(op2), .in1(immx), .out(B), .sel(isImmx));
  Multiplexer #(.width(32)) multiplexer_6 (.in0(op2_t), .in1(data), .out(op2), .sel(PinOP2));  // open: en
  Multiplexer #(.width(32)) multiplexer_7 (.in0(A_t), .in1(data), .out(A), .sel(PinOP1));  // open: en

  // Notes on the sheet:
  //   (Branch Target Calculation)
  //   (27 bit offset)
  //   OF Stage (Edited)
  //   (has Return Address
  //   when instruction is ret)
  //   (Registers from RW Stage moved here to maintain consistency)
  //   rs1
  //   rs2
  //   rd
  //   (modifier bits)
  //   19:22
  //   15:18
  //   23:26
  //   (Immediate Calculation)
  //   (no modifier)
  //   (modifier u)
  //   (modifier h)
  //   (Register Access)
  //   (32 bit modifed immediate)
  //   (OF Outputs)
endmodule

module MA (
  input  [31:0] ALUResult,
  input  isLd,
  input  Clock,
  input  isSt,
  input  [31:0] op2,
  output [31:0] ldResult
);

  wire and_1_out, not_1_out, xor_1_out;
  wire [31:0] shifter_1_out;

  Shifter #(.width(32), .shift("ar")) shifter_1 (.in(ALUResult), .\dist (5'b00010), .out(shifter_1_out));
  and and_1 (and_1_out, isSt, Clock);
  xor xor_1 (xor_1_out, isLd, and_1_out);
  not not_1 (not_1_out, isSt);
  RAM #(.addrWidth(24), .dataWidth(32), .bus("asynch")) ram_1 (
    .addr(shifter_1_out[23:0]), .data(ldResult), .sel(xor_1_out), .ld(not_1_out));  // open: clr
  assign ldResult = isSt ? op2 : 32'bz;  // Controlled_Buffer controlled_buffer_1

  // Notes on the sheet:
  //   MA  Stage
  //   Memory Address
  //   (Data to be stored)
endmodule

module RW (
  input  [31:0] ALUResult,
  input  [31:0] ldResult,
  input  isLd,
  input  [23:0] PC,
  input  isCall,
  input  [31:0] Instruction,
  output [31:0] storeData,
  output [3:0] Address
);

  wire [31:0] adder_1_out, bit_extender_1_out;

  assign bit_extender_1_out = {{8{1'b0}}, PC};  // Bit_Extender bit_extender_1
  Multiplexer #(.width(4), .enable("false")) multiplexer_1 (
    .in0(Instruction[25:22]), .in1(4'b1111), .out(Address), .sel(isCall));
  Adder #(.width(32)) adder_1 (.a(bit_extender_1_out), .b(32'h1), .out(adder_1_out));  // open: cin, cout
  Multiplexer #(.select(2), .width(32), .enable("false")) multiplexer_2 (
    .in0(ALUResult), .in1(ldResult), .in2(adder_1_out), .out(storeData), .sel({isCall, isLd}));  // open: in3

  // Notes on the sheet:
  //   storeData: pull=down
  //   PC: pull=down
  //   Address: pull=down
  //   RW Stage (Edited)
  //   (for arithmetic instructions)
  //   (data loaded from memory)
  //   (to update return address)
  //   (Register to be written to)
  //   (Registers moved to OF Stage to maintain consistency)
  //   (Integer to be written back in register)
endmodule

module regFile (
  input  clock,
  input  [3:0] readA,
  input  [31:0] writeData,
  input  [3:0] readB,
  input  [3:0] writeAddress,
  input  [3:0] displayRead,
  output [31:0] outA,
  output [31:0] outB,
  output [31:0] displayOut
);

  wire counter_1_q;
  wire [31:0] demultiplexer_1_out0, demultiplexer_1_out1, demultiplexer_1_out2, demultiplexer_1_out3,
       demultiplexer_1_out4, demultiplexer_1_out5, demultiplexer_1_out6, demultiplexer_1_out7,
       demultiplexer_1_out8, demultiplexer_1_out9, demultiplexer_1_out10, demultiplexer_1_out11,
       demultiplexer_1_out12, demultiplexer_1_out13, demultiplexer_1_out14, demultiplexer_1_out15,
       multiplexer_1_out, r0, r1, r2, r3, r4, r5, r6, r7, r8, r9, r10, r11, r12, r13, r14, r15;

  Demultiplexer #(.select(4), .width(32), .tristate("true"), .enable("false")) demultiplexer_1 (
    .out0(demultiplexer_1_out0), .out1(demultiplexer_1_out1), .out2(demultiplexer_1_out2),
    .out3(demultiplexer_1_out3), .out4(demultiplexer_1_out4), .out5(demultiplexer_1_out5),
    .out6(demultiplexer_1_out6), .out7(demultiplexer_1_out7), .out8(demultiplexer_1_out8),
    .out9(demultiplexer_1_out9), .out10(demultiplexer_1_out10), .out11(demultiplexer_1_out11),
    .out12(demultiplexer_1_out12), .out13(demultiplexer_1_out13), .out14(demultiplexer_1_out14),
    .out15(demultiplexer_1_out15), .in(writeData), .sel(writeAddress));
  Counter #(.width(1), .max('h1), .ongoal("stay")) counter_1 (
    .Q(counter_1_q), .clk(clock));  // open: load, D, count, carry, clr
  Multiplexer #(.width(32), .enable("false")) multiplexer_1 (
    .in0(32'h3fffffc), .in1(demultiplexer_1_out14), .out(multiplexer_1_out), .sel(counter_1_q));
  Register #(.width(32)) u_r0 (.D(demultiplexer_1_out0), .Q(r0), .clk(clock));  // open: en, clr
  Register #(.width(32)) u_r1 (.D(demultiplexer_1_out1), .Q(r1), .clk(clock));  // open: en, clr
  Register #(.width(32)) u_r2 (.D(demultiplexer_1_out2), .Q(r2), .clk(clock));  // open: en, clr
  Register #(.width(32)) u_r3 (.D(demultiplexer_1_out3), .Q(r3), .clk(clock));  // open: en, clr
  Register #(.width(32)) u_r4 (.D(demultiplexer_1_out4), .Q(r4), .clk(clock));  // open: en, clr
  Register #(.width(32)) u_r5 (.D(demultiplexer_1_out5), .Q(r5), .clk(clock));  // open: en, clr
  Register #(.width(32)) u_r6 (.D(demultiplexer_1_out6), .Q(r6), .clk(clock));  // open: en, clr
  Register #(.width(32)) u_r7 (.D(demultiplexer_1_out7), .Q(r7), .clk(clock));  // open: en, clr
  Register #(.width(32)) u_r8 (.D(demultiplexer_1_out8), .Q(r8), .clk(clock));  // open: en, clr
  Register #(.width(32)) u_r9 (.D(demultiplexer_1_out9), .Q(r9), .clk(clock));  // open: en, clr
  Register #(.width(32)) u_r10 (.D(demultiplexer_1_out10), .Q(r10), .clk(clock));  // open: en, clr
  Register #(.width(32)) u_r11 (.D(demultiplexer_1_out11), .Q(r11), .clk(clock));  // open: en, clr
  Register #(.width(32)) u_r12 (.D(demultiplexer_1_out12), .Q(r12), .clk(clock));  // open: en, clr
  Register #(.width(32)) u_r13 (.D(demultiplexer_1_out13), .Q(r13), .clk(clock));  // open: en, clr
  Register #(.width(32)) u_r14 (.D(multiplexer_1_out), .Q(r14), .clk(clock));  // open: en, clr
  Register #(.width(32)) u_r15 (.D(demultiplexer_1_out15), .Q(r15), .clk(clock));  // open: en, clr
  Multiplexer #(.select(4), .width(32), .disabled(0), .enable("false")) multiplexer_2 (
    .in0(r0), .in1(r1), .in2(r2), .in3(r3), .in4(r4), .in5(r5), .in6(r6), .in7(r7), .in8(r8), .in9(r9),
    .in10(r10), .in11(r11), .in12(r12), .in13(r13), .in14(r14), .in15(r15), .out(outA), .sel(readA));
  Multiplexer #(.select(4), .width(32), .disabled(0), .enable("false")) multiplexer_3 (
    .in0(r0), .in1(r1), .in2(r2), .in3(r3), .in4(r4), .in5(r5), .in6(r6), .in7(r7), .in8(r8), .in9(r9),
    .in10(r10), .in11(r11), .in12(r12), .in13(r13), .in14(r14), .in15(r15), .out(outB), .sel(readB));
  Multiplexer #(.select(4), .width(32), .disabled(0), .enable("false")) multiplexer_4 (
    .in0(r0), .in1(r1), .in2(r2), .in3(r3), .in4(r4), .in5(r5), .in6(r6), .in7(r7), .in8(r8), .in9(r9),
    .in10(r10), .in11(r11), .in12(r12), .in13(r13), .in14(r14), .in15(r15), .out(displayOut),
    .sel(displayRead));

  // Notes on the sheet:
  //   writeAddress: pull=down
  //   outB: pull=down
  //   outA: pull=down
  //   displayRead: pull=down
  //   readA: pull=down
  //   readB: pull=down
  //   writeData: pull=down
  //   displayOut: pull=down
  //   (for RW Stage)
  //   (to initialize stack pointer
  //   to last memory location)
  //   (to fetch Operand 1)
  //   (to fetch Operand 2)
  //   (for external display)
endmodule

module CU (
  input  [31:0] Instruction,
  output isWb,
  output isUbranch,
  output isImmediate,
  output isLd,
  output isSt,
  output isBeq,
  output isBgt,
  output isCall,
  output isRet,
  output [3:0] ALUSignals
);

  wire and_1_out, and_2_out, and_3_out, and_4_out, demultiplexer_1_out0, demultiplexer_1_out1, isAdd, isAnd,
       isAsr, isCmp, isDiv, isLsl, isLsr, isMod, isMov, isMul, isNot, isOr, not_1_out, not_2_out, not_3_out,
       not_4_out, not_5_out, not_6_out, not_7_out, or_1_out, or_2_out;
  wire [3:0] adder_1_out, adder_2_out, adder_3_out, adder_4_out, adder_5_out, adder_6_out, adder_7_out,
       adder_8_out, adder_9_out, adder_10_out, adder_11_out, bit_extender_1_out, bit_extender_2_out,
       bit_extender_3_out, bit_extender_4_out, bit_extender_5_out, bit_extender_6_out, bit_extender_7_out,
       bit_extender_8_out, bit_extender_9_out, bit_extender_10_out, bit_extender_11_out, bit_extender_12_out,
       bit_extender_13_out, multiplier_1_out, multiplier_2_out, multiplier_3_out, multiplier_4_out,
       multiplier_5_out, multiplier_6_out, multiplier_7_out, multiplier_8_out, multiplier_9_out,
       multiplier_10_out, multiplier_11_out, multiplier_12_out;

  not not_1 (not_1_out, Instruction[28]);
  not not_2 (not_2_out, Instruction[29]);
  not not_3 (not_3_out, Instruction[28]);
  not not_4 (not_4_out, Instruction[27]);
  not not_5 (not_5_out, Instruction[31]);
  Demultiplexer #(.select(5), .disabled(0), .enable("false")) demultiplexer_1 (
    .out0(demultiplexer_1_out0), .out1(demultiplexer_1_out1), .out2(isMul), .out3(isDiv), .out4(isMod),
    .out5(isCmp), .out6(isAnd), .out7(isOr), .out8(isNot), .out9(isMov), .out10(isLsl), .out11(isLsr),
    .out12(isAsr), .out14(isLd), .out15(isSt), .out16(isBeq), .out17(isBgt), .out19(isCall), .out20(isRet),
    .in(1'b1), .sel(Instruction[31:27]));  // open: out13, out18, out21, out22, out23, out24, out25, out26, out27, out28, out29, out30, out31
  not not_6 (not_6_out, Instruction[31]);
  or or_1 (or_1_out, Instruction[30], not_1_out);
  and and_1 (and_1_out, not_2_out, Instruction[28]);
  and and_2 (and_2_out, Instruction[29], not_3_out, not_4_out);
  and and_3 (and_3_out, Instruction[28], Instruction[29], Instruction[30], not_5_out);
  and and_4 (and_4_out, not_6_out, Instruction[29], Instruction[27], or_1_out);
  not not_7 (not_7_out, Instruction[30]);
  or or_2 (or_2_out, and_1_out, and_2_out);
  nor nor_1 (isWb, Instruction[31], and_4_out);
  and and_5 (isUbranch, Instruction[31], not_7_out, or_2_out);
  or or_3 (isAdd, and_3_out, demultiplexer_1_out0);
  assign bit_extender_1_out = {{3{1'b0}}, demultiplexer_1_out1};  // Bit_Extender bit_extender_1
  assign bit_extender_2_out = {{3{1'b0}}, isCmp};  // Bit_Extender bit_extender_2
  assign bit_extender_3_out = {{3{1'b0}}, isMul};  // Bit_Extender bit_extender_3
  assign bit_extender_4_out = {{3{1'b0}}, isDiv};  // Bit_Extender bit_extender_4
  assign bit_extender_5_out = {{3{1'b0}}, isMod};  // Bit_Extender bit_extender_5
  assign bit_extender_6_out = {{3{1'b0}}, isLsl};  // Bit_Extender bit_extender_6
  assign bit_extender_7_out = {{3{1'b0}}, isLsr};  // Bit_Extender bit_extender_7
  assign bit_extender_8_out = {{3{1'b0}}, isAsr};  // Bit_Extender bit_extender_8
  assign bit_extender_9_out = {{3{1'b0}}, isOr};  // Bit_Extender bit_extender_9
  assign bit_extender_10_out = {{3{1'b0}}, isNot};  // Bit_Extender bit_extender_10
  assign bit_extender_11_out = {{3{1'b0}}, isAnd};  // Bit_Extender bit_extender_11
  assign bit_extender_12_out = {{3{1'b0}}, isMov};  // Bit_Extender bit_extender_12
  assign bit_extender_13_out = {{3{1'b0}}, isAdd};  // Bit_Extender bit_extender_13
  Multiplier #(.width(4)) multiplier_1 (
    .a(bit_extender_1_out), .b(4'b0010), .out(multiplier_1_out));  // open: cin, cout
  Multiplier #(.width(4)) multiplier_2 (
    .a(bit_extender_2_out), .b(4'b0011), .out(multiplier_2_out));  // open: cin, cout
  Multiplier #(.width(4)) multiplier_3 (
    .a(bit_extender_3_out), .b(4'b0100), .out(multiplier_3_out));  // open: cin, cout
  Multiplier #(.width(4)) multiplier_4 (
    .a(bit_extender_4_out), .b(4'b0101), .out(multiplier_4_out));  // open: cin, cout
  Multiplier #(.width(4)) multiplier_5 (
    .a(bit_extender_5_out), .b(4'b0110), .out(multiplier_5_out));  // open: cin, cout
  Multiplier #(.width(4)) multiplier_6 (
    .a(bit_extender_6_out), .b(4'b0111), .out(multiplier_6_out));  // open: cin, cout
  Multiplier #(.width(4)) multiplier_7 (
    .a(bit_extender_7_out), .b(4'b1000), .out(multiplier_7_out));  // open: cin, cout
  Multiplier #(.width(4)) multiplier_8 (
    .a(bit_extender_8_out), .b(4'b1001), .out(multiplier_8_out));  // open: cin, cout
  Multiplier #(.width(4)) multiplier_9 (
    .a(bit_extender_9_out), .b(4'b1010), .out(multiplier_9_out));  // open: cin, cout
  Multiplier #(.width(4)) multiplier_10 (
    .a(bit_extender_10_out), .b(4'b1011), .out(multiplier_10_out));  // open: cin, cout
  Multiplier #(.width(4)) multiplier_11 (
    .a(bit_extender_11_out), .b(4'b1100), .out(multiplier_11_out));  // open: cin, cout
  Multiplier #(.width(4)) multiplier_12 (
    .a(bit_extender_12_out), .b(4'b1101), .out(multiplier_12_out));  // open: cin, cout
  Adder #(.width(4)) adder_1 (.a(bit_extender_13_out), .b(multiplier_1_out), .out(adder_1_out));  // open: cin, cout
  Adder #(.width(4)) adder_2 (.a(multiplier_2_out), .b(multiplier_3_out), .out(adder_2_out));  // open: cin, cout
  Adder #(.width(4)) adder_3 (.a(multiplier_4_out), .b(multiplier_5_out), .out(adder_3_out));  // open: cin, cout
  Adder #(.width(4)) adder_4 (.a(multiplier_6_out), .b(multiplier_7_out), .out(adder_4_out));  // open: cin, cout
  Adder #(.width(4)) adder_5 (.a(multiplier_8_out), .b(multiplier_9_out), .out(adder_5_out));  // open: cin, cout
  Adder #(.width(4)) adder_6 (.a(multiplier_10_out), .b(multiplier_11_out), .out(adder_6_out));  // open: cin, cout
  Adder #(.width(4)) adder_7 (.a(adder_1_out), .b(adder_2_out), .out(adder_7_out));  // open: cin, cout
  Adder #(.width(4)) adder_8 (.a(adder_3_out), .b(adder_4_out), .out(adder_8_out));  // open: cin, cout
  Adder #(.width(4)) adder_9 (.a(adder_5_out), .b(adder_6_out), .out(adder_9_out));  // open: cin, cout
  Adder #(.width(4)) adder_10 (.a(adder_7_out), .b(adder_8_out), .out(adder_10_out));  // open: cin, cout
  Adder #(.width(4)) adder_11 (.a(adder_9_out), .b(multiplier_12_out), .out(adder_11_out));  // open: cin, cout
  Adder #(.width(4)) adder_12 (.a(adder_10_out), .b(adder_11_out), .out(ALUSignals));  // open: cin, cout

  assign isImmediate = Instruction[26];

  // Notes on the sheet:
  //   Instruction: pull=down
  //   opcode
  //   (Circuit for signals created by multiple instructions)
  //   (Demultiplexer for Control Signals created by single instructions)
  //   Create ALUSignals
endmodule

module ALU (
  input  [31:0] A,
  input  [3:0] aluSignals,
  input  [31:0] B,
  input  clock,
  output [31:0] aluResult,
  output flags_GT,
  output flags_E
);

  wire [31:0] Add, addA, addB, And, andA, andB, Asr, asrA, asrB, cmpA, cmpB, Div, divA, divB, Lsl, lslA,
       lslB, Lsr, lsrA, lsrB, Mod, modA, modB, movB, Mul, mulA, mulB, Not, notB, Or, orA, orB, register_1_q,
       register_2_q, Sub, subA, subB;

  Demultiplexer #(.select(4), .width(32), .tristate("true"), .enable("false")) demultiplexer_1 (
    .out1(addA), .out2(subA), .out3(cmpA), .out4(mulA), .out5(divA), .out6(modA), .out7(lslA), .out8(lsrA),
    .out9(asrA), .out10(orA), .out12(andA), .in(A), .sel(aluSignals));  // open: out0, out11, out13, out14, out15
  Demultiplexer #(.select(4), .width(32), .tristate("true"), .disabled(0), .enable("false")) demultiplexer_2 (
    .out1(addB), .out2(subB), .out3(cmpB), .out4(mulB), .out5(divB), .out6(modB), .out7(lslB), .out8(lsrB),
    .out9(asrB), .out10(orB), .out11(notB), .out12(andB), .out13(movB), .in(B), .sel(aluSignals));  // open: out0, out14, out15
  Adder #(.width(32)) adder_1 (.a(addA), .b(addB), .out(Add));  // open: cin, cout
  Subtractor #(.width(32)) subtractor_1 (.a(subA), .b(subB), .out(Sub));  // open: bin, bout
  Shifter #(.width(32)) shifter_1 (.in(lslA), .\dist (lslB[4:0]), .out(Lsl));
  Shifter #(.width(32), .shift("lr")) shifter_2 (.in(lsrA), .\dist (lsrB[4:0]), .out(Lsr));
  Shifter #(.width(32), .shift("ar")) shifter_3 (.in(asrA), .\dist (asrB[4:0]), .out(Asr));
  Register #(.width(32)) register_1 (.D(cmpA), .Q(register_1_q), .clk(clock));  // open: en, clr
  Register #(.width(32)) register_2 (.D(cmpB), .Q(register_2_q), .clk(clock));  // open: en, clr
  Comparator #(.width(32)) comparator_1 (.a(register_1_q), .b(register_2_q), .gt(flags_GT), .eq(flags_E));  // open: lt
  Multiplier #(.width(32)) multiplier_1 (.a(mulA), .b(mulB), .out(Mul));  // open: cin, cout
  Divider #(.width(32)) divider_1 (.a(divA), .b(divB), .out(Div));  // open: upper, rem
  Divider #(.width(32)) divider_2 (.a(modA), .b(modB), .rem(Mod));  // open: out, upper
  Multiplexer #(.select(4), .width(32), .disabled(0)) multiplexer_1 (
    .in1(Add), .in2(Sub), .in4(Mul), .in5(Div), .in6(Mod), .in7(Lsl), .in8(Lsr), .in9(Asr), .in10(Or),
    .in11(Not), .in12(And), .in13(movB), .out(aluResult), .sel(aluSignals), .en(1'b1));  // open: in0, in3, in14, in15
  assign Or = orA | orB;  // OR_Gate or_1, 32 bits wide
  assign And = andA & andB;  // AND_Gate and_1, 32 bits wide
  assign Not = ~notB;  // NOT_Gate not_1, 32 bits wide

  // Notes on the sheet:
  //   flags_E: pull=down
  //   A: pull=down
  //   B: pull=down
  //   aluResult: pull=down
  //   flags_GT: pull=down
  //   Operand 1
  //   Operand 2
  //   Provide operands to their respective functions.
  //   Compare instruction needs registers as we need to keep the value of the flags stored.
endmodule

module EXU (
  input  isBeq,
  input  isUbranch,
  input  isBgt,
  input  isRet,
  input  [31:0] branchTargetIn,
  input  [31:0] A,
  input  [3:0] aluSignals,
  input  [31:0] B,
  input  Clock,
  output isBranchTaken,
  output [23:0] branchTargetOut,
  output [31:0] ALUResult
);

  wire and_1_out, and_2_out, flags_E, flags_GT;
  wire [31:24] multiplexer_1_out;

  and and_1 (and_1_out, isBeq, flags_E);
  and and_2 (and_2_out, isBgt, flags_GT);
  ALU alu_1 (
    .A(A), .aluSignals(aluSignals), .B(B), .clock(Clock), .aluResult(ALUResult), .flags_GT(flags_GT),
    .flags_E(flags_E));
  Multiplexer #(.width(32), .enable("false")) multiplexer_1 (
    .in0(branchTargetIn), .in1(A), .out({multiplexer_1_out, branchTargetOut}), .sel(isRet));
  or or_1 (isBranchTaken, and_1_out, isUbranch, and_2_out);

  // Notes on the sheet:
  //   aluSignals: pull=down
  //   branchTargetIn: pull=down
  //   isUbranch: pull=down
  //   isBgt: pull=down
  //   branchTargetOut: pull=down
  //   isBranchTaken: pull=down
  //   ALUResult: pull=down
  //   A: pull=down
  //   B: pull=down
  //   isBeq: pull=down
  //   (Operand 1)
  //   (Operand 2)
  //   EX Stage
  //   (To be sent to the IF Stage)
endmodule

module New (
);

  wire alubeq, alubgt, alucall, aluimm, aluld, aluret, alust, aluub, aluwb, button_1_out, clock_1_out, cubeq,
       cubgt, cucall, cuimm, culd, curet, cust, cuub, cuwb, exu_1_isbranchtaken, instrpacket_3_out_isld,
       instrpacket_3_out_isst, instrpacket_4_out_iscall, instrpacket_4_out_isld;
  wire [3:0] Addr, alualu, cualu, undriven;
  wire [23:0] exu_1_branchtargetout, if_1_pc, instrpacket_1_out_pc, instrpacket_2_out_pc,
       instrpacket_3_out_pc, instrpacket_4_out_pc;
  wire [31:0] data, exu_1_aluresult, if_1_instruction, instrpacket_1_out_instr, instrpacket_2_out_a,
       instrpacket_2_out_b, instrpacket_2_out_branchtarget, instrpacket_2_out_instr, instrpacket_2_out_op2,
       instrpacket_3_out_aluresult, instrpacket_3_out_instr, instrpacket_3_out_op2,
       instrpacket_4_out_aluresult, instrpacket_4_out_instr, instrpacket_4_out_ldresult, ma_1_ldresult,
       of_1_a, of_1_b, of_1_branchtarget, of_1_op2;

  Button button_1 (.out(button_1_out));
  Clock clock_1 (.out(clock_1_out));
  IF if_1 (
    .isBranchTaken(exu_1_isbranchtaken), .Instruction(if_1_instruction),
    .branchTarget(exu_1_branchtargetout), .IFstageclock(clock_1_out), .PC(if_1_pc), .reset(button_1_out));
  instrPacket instrpacket_1 (
    .in_PC(if_1_pc), .in_Instr(if_1_instruction), .out_PC(instrpacket_1_out_pc),
    .out_Instr(instrpacket_1_out_instr), .in_CLK(clock_1_out), .Reset(button_1_out));  // open: in_BranchTarget, in_ldResult, in_aluResult, in_B, in_A, in_op2, in_isWB, in_isUBranch, in_isImmediate, in_aluSignals, in_isLd, in_isBeq, in_isRet, in_isCall, in_isBgt, in_isSt, out_BranchTarget, out_OpCode, out_LdResult, out_aluResult, out_B, out_A, out_op2, out_isWB, out_isUBranch, out_isImmediate, out_aluSignals, out_isLd, out_isBeq, out_isRet, out_isCall, out_isBgt, out_isSt
  CU cu_1 (
    .isWb(cuwb), .isUbranch(cuub), .isImmediate(cuimm), .isLd(culd), .isSt(cust), .isBeq(cubeq),
    .isBgt(cubgt), .isCall(cucall), .isRet(curet), .ALUSignals(cualu), .Instruction(instrpacket_1_out_instr));
  OF of_1 (
    .Instruction(instrpacket_1_out_instr), .PC(instrpacket_1_out_pc), .branchTarget(of_1_branchtarget),
    .isSt(cust), .isImmx(cuimm), .A(of_1_a), .B(of_1_b), .op2(of_1_op2), .isRet(curet), .writeData(data),
    .writeAddress(undriven), .clock(clock_1_out));  // open: isWb, displayAddress, displayOut, isCall, data, PinOP2, PinOP1
  instrPacket instrpacket_2 (
    .in_PC(instrpacket_1_out_pc), .in_BranchTarget(of_1_branchtarget), .in_Instr(instrpacket_1_out_instr),
    .in_B(of_1_b), .in_A(of_1_a), .in_op2(of_1_op2), .in_isWB(cuwb), .in_isUBranch(cuub),
    .in_isImmediate(cuimm), .in_aluSignals(cualu), .in_isLd(culd), .in_isBeq(cubeq), .in_isRet(curet),
    .in_isCall(cucall), .in_isBgt(cubgt), .in_isSt(cust), .out_PC(instrpacket_2_out_pc),
    .out_BranchTarget(instrpacket_2_out_branchtarget), .out_Instr(instrpacket_2_out_instr),
    .out_B(instrpacket_2_out_b), .out_A(instrpacket_2_out_a), .out_op2(instrpacket_2_out_op2),
    .out_isWB(aluwb), .out_isUBranch(aluub), .out_isImmediate(aluimm), .out_aluSignals(alualu),
    .out_isLd(aluld), .out_isBeq(alubeq), .out_isRet(aluret), .out_isCall(alucall), .out_isBgt(alubgt),
    .out_isSt(alust), .in_CLK(clock_1_out), .Reset(button_1_out));  // open: in_ldResult, in_aluResult, out_OpCode, out_LdResult, out_aluResult
  EXU exu_1 (
    .isBeq(alubeq), .isUbranch(aluub), .isBgt(alubgt), .branchTargetIn(instrpacket_2_out_branchtarget),
    .A(instrpacket_2_out_a), .aluSignals(alualu), .B(instrpacket_2_out_b), .Clock(clock_1_out),
    .isBranchTaken(exu_1_isbranchtaken), .branchTargetOut(exu_1_branchtargetout),
    .ALUResult(exu_1_aluresult), .isRet(aluret));
  instrPacket instrpacket_3 (
    .in_PC(instrpacket_2_out_pc), .in_Instr(instrpacket_2_out_instr), .in_aluResult(exu_1_aluresult),
    .in_op2(instrpacket_2_out_op2), .in_isWB(aluwb), .in_isUBranch(aluub), .in_isImmediate(aluimm),
    .in_aluSignals(alualu), .in_isLd(aluld), .in_isBeq(alubeq), .in_isRet(aluret), .in_isCall(alucall),
    .in_isBgt(alubgt), .in_isSt(alust), .out_PC(instrpacket_3_out_pc), .out_Instr(instrpacket_3_out_instr),
    .out_aluResult(instrpacket_3_out_aluresult), .out_op2(instrpacket_3_out_op2),
    .out_isLd(instrpacket_3_out_isld), .out_isSt(instrpacket_3_out_isst), .in_CLK(clock_1_out),
    .Reset(button_1_out));  // open: in_BranchTarget, in_ldResult, in_B, in_A, out_BranchTarget, out_OpCode, out_LdResult, out_B, out_A, out_isWB, out_isUBranch, out_isImmediate, out_aluSignals, out_isBeq, out_isRet, out_isCall, out_isBgt
  MA ma_1 (
    .ldResult(ma_1_ldresult), .op2(instrpacket_3_out_op2), .isLd(instrpacket_3_out_isld),
    .isSt(instrpacket_3_out_isst), .ALUResult(instrpacket_3_out_aluresult), .Clock(clock_1_out));
  instrPacket instrpacket_4 (
    .in_PC(instrpacket_3_out_pc), .in_Instr(instrpacket_3_out_instr), .in_ldResult(ma_1_ldresult),
    .out_PC(instrpacket_4_out_pc), .out_Instr(instrpacket_4_out_instr),
    .out_LdResult(instrpacket_4_out_ldresult), .out_aluResult(instrpacket_4_out_aluresult),
    .out_isLd(instrpacket_4_out_isld), .out_isCall(instrpacket_4_out_iscall), .in_CLK(clock_1_out),
    .Reset(button_1_out));  // open: in_BranchTarget, in_aluResult, in_B, in_A, in_op2, in_isWB, in_isUBranch, in_isImmediate, in_aluSignals, in_isLd, in_isBeq, in_isRet, in_isCall, in_isBgt, in_isSt, out_BranchTarget, out_OpCode, out_B, out_A, out_op2, out_isWB, out_isUBranch, out_isImmediate, out_aluSignals, out_isBeq, out_isRet, out_isBgt, out_isSt
  RW rw_1 (
    .Instruction(instrpacket_4_out_instr), .ldResult(instrpacket_4_out_ldresult),
    .isLd(instrpacket_4_out_isld), .ALUResult(instrpacket_4_out_aluresult),
    .isCall(instrpacket_4_out_iscall), .PC(instrpacket_4_out_pc), .Address(Addr), .storeData(data));
endmodule

module instrPacket (
  input  [23:0] in_PC,
  input  [31:0] in_BranchTarget,
  input  [31:0] in_Instr,
  input  [31:0] in_ldResult,
  input  [31:0] in_aluResult,
  input  [31:0] in_B,
  input  [31:0] in_A,
  input  [31:0] in_op2,
  input  in_CLK,
  input  Reset,
  input  in_isWB,
  input  in_isUBranch,
  input  in_isImmediate,
  input  [3:0] in_aluSignals,
  input  in_isLd,
  input  in_isBeq,
  input  in_isRet,
  input  in_isCall,
  input  in_isBgt,
  input  in_isSt,
  output [23:0] out_PC,
  output [31:0] out_BranchTarget,
  output [31:0] out_Instr,
  output [4:0] out_OpCode,
  output [31:0] out_LdResult,
  output [31:0] out_aluResult,
  output [31:0] out_B,
  output [31:0] out_A,
  output [31:0] out_op2,
  output out_isWB,
  output out_isUBranch,
  output out_isImmediate,
  output [3:0] out_aluSignals,
  output out_isLd,
  output out_isBeq,
  output out_isRet,
  output out_isCall,
  output out_isBgt,
  output out_isSt
);

  Register #(.width(24)) PC (.D(in_PC), .en(in_CLK), .Q(out_PC), .clk(in_CLK), .clr(Reset));
  Register #(.width(32)) Branch_Target (
    .D(in_BranchTarget), .en(in_CLK), .Q(out_BranchTarget), .clk(in_CLK), .clr(Reset));
  Register #(.width(32)) Instr (.D(in_Instr), .en(in_CLK), .Q(out_Instr), .clk(in_CLK), .clr(Reset));
  Register #(.width(5)) OpCode (.D(in_Instr[31:27]), .en(in_CLK), .Q(out_OpCode), .clk(in_CLK), .clr(Reset));
  Register #(.width(32)) ldResult (.D(in_ldResult), .en(in_CLK), .Q(out_LdResult), .clk(in_CLK), .clr(Reset));
  Register #(.width(32)) aluResult (.D(in_aluResult), .en(in_CLK), .Q(out_aluResult), .clk(in_CLK), .clr(Reset));
  Register #(.width(32)) B (.D(in_B), .en(in_CLK), .Q(out_B), .clk(in_CLK), .clr(Reset));
  Register #(.width(32)) A (.D(in_A), .en(in_CLK), .Q(out_A), .clk(in_CLK), .clr(Reset));
  Register #(.width(32)) op2 (.D(in_op2), .en(in_CLK), .Q(out_op2), .clk(in_CLK), .clr(Reset));
  Register #(.width(1)) isWB (.D(in_isWB), .en(in_CLK), .Q(out_isWB), .clk(in_CLK), .clr(Reset));
  Register #(.width(1)) isUBranch (.D(in_isUBranch), .en(in_CLK), .Q(out_isUBranch), .clk(in_CLK), .clr(Reset));
  Register #(.width(1)) isImmediate (.D(in_isImmediate), .en(in_CLK), .Q(out_isImmediate), .clk(in_CLK), .clr(Reset));
  Register #(.width(4)) aluSignals (.D(in_aluSignals), .en(in_CLK), .Q(out_aluSignals), .clk(in_CLK), .clr(Reset));
  Register #(.width(1)) isLd (.D(in_isLd), .en(in_CLK), .Q(out_isLd), .clk(in_CLK), .clr(Reset));
  Register #(.width(1)) isBeq (.D(in_isBeq), .en(in_CLK), .Q(out_isBeq), .clk(in_CLK), .clr(Reset));
  Register #(.width(1)) isRet (.D(in_isRet), .en(in_CLK), .Q(out_isRet), .clk(in_CLK), .clr(Reset));
  Register #(.width(1)) isCall (.D(in_isCall), .en(in_CLK), .Q(out_isCall), .clk(in_CLK), .clr(Reset));
  Register #(.width(1)) isBgt (.D(in_isBgt), .en(in_CLK), .Q(out_isBgt), .clk(in_CLK), .clr(Reset));
  Register #(.width(1)) isSt (.D(in_isSt), .en(in_CLK), .Q(out_isSt), .clk(in_CLK), .clr(Reset));

  // Notes on the sheet:
  //   Instruction Packet
  //   Instruction Related
  //   Numerical
  //   Control
endmodule

module Algo7 (
  input  [31:0] A,
  input  [31:0] B,
  output out_3
);

  wire and_1_out, comparator_1_eq, comparator_2_eq, comparator_3_eq, comparator_4_eq, comparator_5_eq,
       comparator_6_eq, comparator_7_eq, comparator_8_eq, comparator_9_eq, comparator_10_eq,
       comparator_11_eq, comparator_12_eq, comparator_13_eq, comparator_14_eq, comparator_15_eq, not_1_out,
       not_2_out, or_1_out, or_2_out, or_3_out;
  wire [3:0] multiplexer_1_out, multiplexer_2_out;

  Comparator #(.width(5)) comparator_1 (.a(5'b01111), .b(A[31:27]), .eq(comparator_1_eq));  // open: gt, lt
  not not_1 (not_1_out, comparator_1_eq);
  Comparator #(.width(5)) comparator_2 (.a(A[31:27]), .b(5'b01101), .eq(comparator_2_eq));  // open: gt, lt
  Comparator #(.width(5)) comparator_3 (.a(A[31:27]), .b(5'b10000), .eq(comparator_3_eq));  // open: gt, lt
  Comparator #(.width(5)) comparator_4 (.a(A[31:27]), .b(5'b10001), .eq(comparator_4_eq));  // open: gt, lt
  Comparator #(.width(5)) comparator_5 (.a(A[31:27]), .b(5'b10010), .eq(comparator_5_eq));  // open: gt, lt
  Comparator #(.width(5)) comparator_6 (.a(A[31:27]), .b(5'b10011), .eq(comparator_6_eq));  // open: gt, lt
  Multiplexer #(.width(4)) multiplexer_1 (
    .in0(A[25:22]), .in1(A[17:14]), .out(multiplexer_1_out), .sel(not_1_out));  // open: en
  Comparator #(.width(5)) comparator_7 (.a(5'b10011), .b(B[31:27]), .eq(comparator_7_eq));  // open: gt, lt
  Comparator #(.width(5)) comparator_8 (.a(B[31:27]), .b(5'b01101), .eq(comparator_8_eq));  // open: gt, lt
  Comparator #(.width(5)) comparator_9 (.a(B[31:27]), .b(5'b00101), .eq(comparator_9_eq));  // open: gt, lt
  Comparator #(.width(5)) comparator_10 (.a(B[31:27]), .b(5'b01111), .eq(comparator_10_eq));  // open: gt, lt
  Comparator #(.width(5)) comparator_11 (.a(B[31:27]), .b(5'b10000), .eq(comparator_11_eq));  // open: gt, lt
  Comparator #(.width(5)) comparator_12 (.a(B[31:27]), .b(5'b10001), .eq(comparator_12_eq));  // open: gt, lt
  Comparator #(.width(5)) comparator_13 (.a(B[31:27]), .b(5'b10010), .eq(comparator_13_eq));  // open: gt, lt
  Comparator #(.width(5)) comparator_14 (.a(B[31:27]), .b(5'b10100), .eq(comparator_14_eq));  // open: gt, lt
  or or_1 (or_1_out, comparator_2_eq, comparator_3_eq, comparator_4_eq, comparator_5_eq, comparator_6_eq);
  Multiplexer #(.width(4)) multiplexer_2 (
    .in0(B[25:22]), .in1(4'b1111), .out(multiplexer_2_out), .sel(comparator_7_eq));  // open: en
  and and_1 (and_1_out, A[26], not_1_out);
  or or_2 (or_2_out, comparator_8_eq, comparator_9_eq, comparator_10_eq, comparator_11_eq, comparator_12_eq, comparator_13_eq, comparator_14_eq);
  or or_3 (or_3_out, and_1_out, or_1_out, or_2_out);
  Comparator #(.width(4)) comparator_15 (
    .a(multiplexer_1_out), .b(multiplexer_2_out), .eq(comparator_15_eq));  // open: gt, lt
  not not_2 (not_2_out, or_3_out);
  and and_2 (out_3, not_2_out, comparator_15_eq);
endmodule

module Algo6 (
  input  [31:0] A,
  input  [31:0] B,
  output out_3
);

  wire comparator_1_eq, comparator_2_eq, comparator_3_eq, comparator_4_eq, comparator_5_eq, comparator_6_eq,
       comparator_7_eq, comparator_8_eq, comparator_9_eq, comparator_10_eq, comparator_11_eq,
       comparator_12_eq, comparator_13_eq, comparator_14_eq, comparator_15_eq, not_1_out, or_1_out, or_2_out,
       or_3_out;
  wire [3:0] multiplexer_1_out, multiplexer_2_out;

  Comparator #(.width(5)) comparator_1 (.a(5'b10100), .b(A[31:27]), .eq(comparator_1_eq));  // open: gt, lt
  Comparator #(.width(5)) comparator_2 (.a(A[31:27]), .b(5'b01101), .eq(comparator_2_eq));  // open: gt, lt
  Comparator #(.width(5)) comparator_3 (.a(A[31:27]), .b(5'b10000), .eq(comparator_3_eq));  // open: gt, lt
  Comparator #(.width(5)) comparator_4 (.a(A[31:27]), .b(5'b10001), .eq(comparator_4_eq));  // open: gt, lt
  Comparator #(.width(5)) comparator_5 (.a(A[31:27]), .b(5'b10010), .eq(comparator_5_eq));  // open: gt, lt
  Comparator #(.width(5)) comparator_6 (.a(A[31:27]), .b(5'b10011), .eq(comparator_6_eq));  // open: gt, lt
  Comparator #(.width(5)) comparator_7 (.a(B[31:27]), .b(5'b10011), .eq(comparator_7_eq));  // open: gt, lt
  Comparator #(.width(5)) comparator_8 (.a(B[31:27]), .b(5'b01101), .eq(comparator_8_eq));  // open: gt, lt
  Comparator #(.width(5)) comparator_9 (.a(B[31:27]), .b(5'b00101), .eq(comparator_9_eq));  // open: gt, lt
  Comparator #(.width(5)) comparator_10 (.a(B[31:27]), .b(5'b01111), .eq(comparator_10_eq));  // open: gt, lt
  Comparator #(.width(5)) comparator_11 (.a(B[31:27]), .b(5'b10000), .eq(comparator_11_eq));  // open: gt, lt
  Comparator #(.width(5)) comparator_12 (.a(B[31:27]), .b(5'b10001), .eq(comparator_12_eq));  // open: gt, lt
  Comparator #(.width(5)) comparator_13 (.a(B[31:27]), .b(5'b10010), .eq(comparator_13_eq));  // open: gt, lt
  Comparator #(.width(5)) comparator_14 (.a(B[31:27]), .b(5'b10100), .eq(comparator_14_eq));  // open: gt, lt
  Multiplexer #(.width(4)) multiplexer_1 (
    .in0(A[21:18]), .in1(4'b1111), .out(multiplexer_1_out), .sel(comparator_1_eq));  // open: en
  Multiplexer #(.width(4)) multiplexer_2 (
    .in0(B[25:22]), .in1(4'b1111), .out(multiplexer_2_out), .sel(comparator_7_eq));  // open: en
  or or_1 (or_1_out, comparator_2_eq, comparator_3_eq, comparator_4_eq, comparator_5_eq, comparator_6_eq);
  or or_2 (or_2_out, comparator_8_eq, comparator_9_eq, comparator_10_eq, comparator_11_eq, comparator_12_eq, comparator_13_eq, comparator_14_eq);
  or or_3 (or_3_out, or_1_out, or_2_out);
  not not_1 (not_1_out, or_3_out);
  Comparator #(.width(4)) comparator_15 (
    .a(multiplexer_1_out), .b(multiplexer_2_out), .eq(comparator_15_eq));  // open: gt, lt
  and and_1 (out_3, not_1_out, comparator_15_eq);
endmodule

module instrPack2 (
  input  [23:0] in_PC,
  input  [31:0] in_BranchTarget,
  input  [31:0] in_Instr,
  input  [31:0] in_ldResult,
  input  [31:0] in_aluResult,
  input  [31:0] in_B,
  input  [31:0] in_A,
  input  [31:0] in_op2,
  input  in_CLK,
  input  Reset,
  input  in_isWB,
  input  in_isUBranch,
  input  in_isImmediate,
  input  [3:0] in_aluSignals,
  input  in_isLd,
  input  in_isBeq,
  input  in_isRet,
  input  in_isCall,
  input  in_isBgt,
  input  in_isSt,
  output [23:0] out_PC,
  output [31:0] out_BranchTarget,
  output [31:0] out_Instr,
  output [4:0] out_OpCode,
  output [31:0] out_LdResult,
  output [31:0] out_aluResult,
  output [31:0] out_B,
  output [31:0] out_A,
  output [31:0] out_op2,
  output out_isWB,
  output out_isUBranch,
  output out_isImmediate,
  output [3:0] out_aluSignals,
  output out_isLd,
  output out_isBeq,
  output out_isRet,
  output out_isCall,
  output out_isBgt,
  output out_isSt
);

  Register #(.width(24)) PC (.D(in_PC), .en(in_CLK), .Q(out_PC), .clk(in_CLK), .clr(Reset));
  Register #(.width(32)) Branch_Target (
    .D(in_BranchTarget), .en(in_CLK), .Q(out_BranchTarget), .clk(in_CLK), .clr(Reset));
  Register #(.width(32)) Instr (.D(in_Instr), .en(in_CLK), .Q(out_Instr), .clk(in_CLK), .clr(Reset));
  Register #(.width(5)) OpCode (.D(in_Instr[31:27]), .en(in_CLK), .Q(out_OpCode), .clk(in_CLK), .clr(Reset));
  Register #(.width(32)) ldResult (.D(in_ldResult), .en(in_CLK), .Q(out_LdResult), .clk(in_CLK), .clr(Reset));
  Register #(.width(32)) aluResult (.D(in_aluResult), .en(in_CLK), .Q(out_aluResult), .clk(in_CLK), .clr(Reset));
  Register #(.width(32)) B (.D(in_B), .en(in_CLK), .Q(out_B), .clk(in_CLK), .clr(Reset));
  Register #(.width(32)) A (.D(in_A), .en(in_CLK), .Q(out_A), .clk(in_CLK), .clr(Reset));
  Register #(.width(32)) op2 (.D(in_op2), .en(in_CLK), .Q(out_op2), .clk(in_CLK), .clr(Reset));
  Register #(.width(1)) isWB (.D(in_isWB), .en(in_CLK), .Q(out_isWB), .clk(in_CLK), .clr(Reset));
  Register #(.width(1)) isUBranch (.D(in_isUBranch), .en(in_CLK), .Q(out_isUBranch), .clk(in_CLK), .clr(Reset));
  Register #(.width(1)) isImmediate (.D(in_isImmediate), .en(in_CLK), .Q(out_isImmediate), .clk(in_CLK), .clr(Reset));
  Register #(.width(4)) aluSignals (.D(in_aluSignals), .en(in_CLK), .Q(out_aluSignals), .clk(in_CLK), .clr(Reset));
  Register #(.width(1)) isLd (.D(in_isLd), .en(in_CLK), .Q(out_isLd), .clk(in_CLK), .clr(Reset));
  Register #(.width(1)) isBeq (.D(in_isBeq), .en(in_CLK), .Q(out_isBeq), .clk(in_CLK), .clr(Reset));
  Register #(.width(1)) isRet (.D(in_isRet), .en(in_CLK), .Q(out_isRet), .clk(in_CLK), .clr(Reset));
  Register #(.width(1)) isCall (.D(in_isCall), .en(in_CLK), .Q(out_isCall), .clk(in_CLK), .clr(Reset));
  Register #(.width(1)) isBgt (.D(in_isBgt), .en(in_CLK), .Q(out_isBgt), .clk(in_CLK), .clr(Reset));
  Register #(.width(1)) isSt (.D(in_isSt), .en(in_CLK), .Q(out_isSt), .clk(in_CLK), .clr(Reset));

  // Notes on the sheet:
  //   Instruction Packet
  //   Instruction Related
  //   Numerical
  //   Control
endmodule

module NewHope (
  input  [3:0] in_1,
  output [31:0] out_2
);

  wire and_1_out, bls, clk, forwardingunit_1_rw_maf, forwardingunit_1_rw_ofop1, forwardingunit_1_rw_ofop2,
       isWriteBack, ldusestall, not_1_out, not_2_out, not_3_out;
  wire [1:0] forwardingunit_1_rw_exop1, forwardingunit_1_rw_exop2;
  wire [3:0] Addr, Control_2_q_2, cu_1_alusignals;
  wire [12:0] Control_2_q, Control_3_q, Control_q, cu_1_iswb, multiplexer_1_out;
  wire [23:0] exu_1_branchtargetout, if_1_pc, PC_2_q, PC_3_q, PC_4_q, PC_q;
  wire [31:0] A_q, aluResult_2_q, aluResult_q, B_q, BranchTarget_q, Data, DispVal, exu_1_aluresult,
       if_1_instruction, instruction_2_q, instruction_3_q, Instruction_q, ldResult_q, ma_1_ldresult,
       multiplexer_2_out, multiplexer_3_out, multiplexer_4_out, multiplexer_5_out, multiplexer_6_out, of_1_a,
       of_1_b, of_1_branchtarget, of_1_op2, op2_2_q, op2_q;

  Clock clock_1 (.out(clk));
  IF if_1 (
    .isBranchTaken(bls), .Instruction(if_1_instruction), .branchTarget(exu_1_branchtargetout),
    .IFstageclock(and_1_out), .PC(if_1_pc));  // open: reset
  and and_1 (and_1_out, clk, not_1_out);
  not not_1 (not_1_out, ldusestall);
  Hex_Digit_Display hex_digit_display_1 (.value(DispVal[31:28]));  // open: dp
  Register #(.width(32)) INSTR (.D(if_1_instruction), .Q(out_2), .clk(and_1_out));  // open: en, clr
  Register #(.width(24)) PC (.D(if_1_pc), .Q(PC_q), .clk(and_1_out));  // open: en, clr
  Hex_Digit_Display hex_digit_display_2 (.value(DispVal[23:20]));  // open: dp
  Hex_Digit_Display hex_digit_display_3 (.value(DispVal[27:24]));  // open: dp
  Hex_Digit_Display hex_digit_display_4 (.value(DispVal[15:12]));  // open: dp
  Hex_Digit_Display hex_digit_display_5 (.value(DispVal[19:16]));  // open: dp
  CU cu_1 (
    .isWb(cu_1_iswb[0]), .isUbranch(cu_1_iswb[1]), .isImmediate(cu_1_iswb[2]), .isLd(cu_1_iswb[7]),
    .isSt(cu_1_iswb[12]), .isBeq(cu_1_iswb[8]), .isBgt(cu_1_iswb[11]), .isCall(cu_1_iswb[10]),
    .isRet(cu_1_iswb[9]), .ALUSignals(cu_1_alusignals), .Instruction(out_2));
  OF of_1 (
    .Instruction(out_2), .PC(PC_q), .branchTarget(of_1_branchtarget), .isSt(cu_1_iswb[12]),
    .isImmx(cu_1_iswb[2]), .A(of_1_a), .B(of_1_b), .op2(of_1_op2), .isRet(cu_1_iswb[9]), .writeData(Data),
    .writeAddress(Addr), .isWb(isWriteBack), .clock(clk), .displayAddress(in_1), .displayOut(DispVal),
    .isCall(cu_1_iswb[10]), .data(Data), .PinOP2(forwardingunit_1_rw_ofop2),
    .PinOP1(forwardingunit_1_rw_ofop1));
  Hex_Digit_Display hex_digit_display_6 (.value(DispVal[7:4]));  // open: dp
  Hex_Digit_Display hex_digit_display_7 (.value(DispVal[11:8]));  // open: dp
  Hex_Digit_Display hex_digit_display_8 (.value(DispVal[3:0]));  // open: dp
  Multiplexer #(.width(13)) multiplexer_1 (
    .in0({13{1'b0}}), .in1({cu_1_iswb[12:7], cu_1_alusignals, cu_1_iswb[2:0]}), .out(multiplexer_1_out),
    .sel(not_2_out));  // open: en
  not not_2 (not_2_out, bls);
  Multiplexer #(.width(32)) multiplexer_2 (
    .in0(32'h68000000), .in1(out_2), .out(multiplexer_2_out), .sel(not_2_out));  // open: en
  Register #(.width(13)) Control (.D(multiplexer_1_out), .Q(Control_q), .clk(clk));  // open: en, clr
  Register #(.width(32)) Instruction (.D(multiplexer_2_out), .Q(Instruction_q), .clk(clk));  // open: en, clr
  Register #(.width(32)) op2 (.D(of_1_op2), .Q(op2_q), .clk(clk));  // open: en, clr
  Register #(.width(32)) A (.D(of_1_a), .Q(A_q), .clk(clk));  // open: en, clr
  Register #(.width(32)) B (.D(of_1_b), .Q(B_q), .clk(clk));  // open: en, clr
  Register #(.width(32)) BranchTarget (.D(of_1_branchtarget), .Q(BranchTarget_q), .clk(clk));  // open: en, clr
  Register #(.width(24)) PC_2 (.D(PC_q), .Q(PC_2_q), .clk(clk));  // open: en, clr
  loadUseDetect loadusedetect_1 (.IFOF(out_2), .OFEX(Instruction_q), .Stall(ldusestall));
  Multiplexer #(.width(32)) multiplexer_3 (.in0(Data), .in1(op2_q), .out(multiplexer_3_out));  // open: sel, en
  Multiplexer #(.select(2), .width(32)) multiplexer_4 (
    .in0(A_q), .in1(Data), .in2(aluResult_q), .in3(aluResult_q), .out(multiplexer_4_out),
    .sel(forwardingunit_1_rw_exop1));  // open: en
  Multiplexer #(.select(2), .width(32)) multiplexer_5 (
    .in0(B_q), .in1(Data), .in2(aluResult_q), .in3(aluResult_q), .out(multiplexer_5_out),
    .sel(forwardingunit_1_rw_exop2));  // open: en
  EXU exu_1 (
    .isBeq(Control_q[8]), .isUbranch(Control_q[1]), .isBgt(Control_q[11]), .branchTargetIn(BranchTarget_q),
    .A(multiplexer_4_out), .aluSignals(Control_q[6:3]), .B(multiplexer_5_out), .Clock(clk),
    .isBranchTaken(bls), .branchTargetOut(exu_1_branchtargetout), .ALUResult(exu_1_aluresult),
    .isRet(Control_q[9]));
  ForwardingUnit forwardingunit_1 (
    .IFOF(out_2), .OFEX(Instruction_q), .EXMA(instruction_2_q), .MARW(instruction_3_q),
    .MA_EXOP2(forwardingunit_1_rw_exop2[1]), .MA_EXOP1(forwardingunit_1_rw_exop1[1]),
    .RW_OFOP2(forwardingunit_1_rw_ofop2), .RW_OFOP1(forwardingunit_1_rw_ofop1),
    .RW_EXOP2(forwardingunit_1_rw_exop2[0]), .RW_EXOP1(forwardingunit_1_rw_exop1[0]),
    .RW_MAF(forwardingunit_1_rw_maf));
  Register #(.width(13)) Control_2 (
    .D(Control_q), .Q({Control_2_q[12:7], Control_2_q_2, Control_2_q[2:0]}), .clk(clk));  // open: en, clr
  Register #(.width(32)) instruction_2 (.D(Instruction_q), .Q(instruction_2_q), .clk(clk));  // open: en, clr
  Register #(.width(32)) op2_2 (.D(multiplexer_3_out), .Q(op2_2_q), .clk(clk));  // open: en, clr
  Register #(.width(32)) aluResult (.D(exu_1_aluresult), .Q(aluResult_q), .clk(clk));  // open: en, clr
  Register #(.width(24)) PC_3 (.D(PC_2_q), .Q(PC_3_q), .clk(clk));  // open: en, clr
  Multiplexer #(.width(32)) multiplexer_6 (
    .in0(Data), .in1(op2_2_q), .out(multiplexer_6_out), .sel(forwardingunit_1_rw_maf));  // open: en
  MA ma_1 (
    .ldResult(ma_1_ldresult), .op2(multiplexer_6_out), .isLd(Control_2_q[7]), .isSt(Control_2_q[12]),
    .ALUResult(aluResult_q), .Clock(clk));
  Register #(.width(13)) Control_3 (
    .D({Control_2_q[12:7], Control_2_q_2, Control_2_q[2:0]}), .Q(Control_3_q), .clk(clk));  // open: en, clr
  Register #(.width(32)) instruction_3 (.D(instruction_2_q), .Q(instruction_3_q), .clk(clk));  // open: en, clr
  Register #(.width(32)) aluResult_2 (.D(aluResult_q), .Q(aluResult_2_q), .clk(clk));  // open: en, clr
  Register #(.width(32)) ldResult (.D(ma_1_ldresult), .Q(ldResult_q), .clk(clk));  // open: en, clr
  Register #(.width(24)) PC_4 (.D(PC_3_q), .Q(PC_4_q), .clk(clk));  // open: en, clr
  and and_2 (isWriteBack, Control_3_q[0], not_3_out);
  RW rw_1 (
    .Instruction(instruction_3_q), .ldResult(ldResult_q), .isLd(Control_3_q[7]), .ALUResult(aluResult_2_q),
    .isCall(Control_3_q[10]), .PC(PC_4_q), .Address(Addr), .storeData(Data));
  not not_3 (not_3_out, clk);

  // Other names for the same wires on the sheet: nDispReg[3:0] = in_1
endmodule

// MA-EX
module ForwardingUnit (
  input  [31:0] IFOF,
  input  [31:0] OFEX,
  input  [31:0] EXMA,
  input  [31:0] MARW,
  output MA_EXOP2,
  output MA_EXOP1,
  output RW_OFOP2,
  output RW_OFOP1,
  output RW_EXOP2,
  output RW_EXOP1,
  output RW_MAF
);

  wire algo6_1_out_3, algo7_1_out_3, algo7_4_out_3, and_4_out, and_5_out, comparator_1_eq, comparator_2_eq,
       comparator_3_eq, comparator_4_eq, not_1_out;

  Algo7 algo7_1 (.A(OFEX), .B(EXMA), .out_3(algo7_1_out_3));
  and and_1 (MA_EXOP2, not_1_out, algo7_1_out_3);
  Algo6 algo6_1 (.A(OFEX), .B(EXMA), .out_3(algo6_1_out_3));
  and and_2 (MA_EXOP1, not_1_out, algo6_1_out_3);
  Algo7 algo7_2 (.A(IFOF), .B(MARW), .out_3(RW_OFOP2));
  Algo6 algo6_2 (.A(IFOF), .B(MARW), .out_3(RW_OFOP1));
  Algo7 algo7_3 (.A(OFEX), .B(MARW), .out_3(RW_EXOP2));
  Algo6 algo6_3 (.A(OFEX), .B(MARW), .out_3(RW_EXOP1));
  Algo7 algo7_4 (.A(EXMA), .B(MARW), .out_3(algo7_4_out_3));
  and and_3 (RW_MAF, algo7_4_out_3, and_5_out);
  Comparator #(.width(5)) comparator_1 (.a(5'b01111), .b(OFEX[31:27]), .eq(comparator_1_eq));  // open: gt, lt
  Comparator #(.width(5)) comparator_2 (.a(EXMA[31:27]), .b(5'b01110), .eq(comparator_2_eq));  // open: gt, lt
  Comparator #(.width(5)) comparator_3 (.a(5'b01111), .b(EXMA[31:27]), .eq(comparator_3_eq));  // open: gt, lt
  Comparator #(.width(5)) comparator_4 (.a(MARW[31:27]), .b(5'b01110), .eq(comparator_4_eq));  // open: gt, lt
  not not_1 (not_1_out, and_4_out);
  and and_4 (and_4_out, comparator_1_eq, comparator_2_eq);
  and and_5 (and_5_out, comparator_3_eq, comparator_4_eq);
endmodule

module loadUseDetect (
  input  [31:0] IFOF,
  input  [31:0] OFEX,
  output Stall
);

  wire algo6_1_out_3, algo7_1_out_3, and_1_out, comparator_1_eq, comparator_2_eq, not_1_out, or_1_out;

  Comparator #(.width(5)) comparator_1 (.a(5'b01111), .b(IFOF[31:27]), .eq(comparator_1_eq));  // open: gt, lt
  Algo6 algo6_1 (.A(IFOF), .B(OFEX), .out_3(algo6_1_out_3));
  Algo7 algo7_1 (.A(IFOF), .B(OFEX), .out_3(algo7_1_out_3));
  Comparator #(.width(5)) comparator_2 (.a(OFEX[31:27]), .b(5'b01110), .eq(comparator_2_eq));  // open: gt, lt
  not not_1 (not_1_out, comparator_1_eq);
  or or_1 (or_1_out, algo6_1_out_3, algo7_1_out_3);
  and and_1 (and_1_out, not_1_out, comparator_2_eq);
  and and_2 (Stall, or_1_out, and_1_out);

  // Notes on the sheet:
  //   is it a store?
  //   is it a load?
endmodule

module TheEmpireStrikesBack (
  input  [3:0] in_1,
  output [31:0] out_2
);

  wire and_1_out, bls, clk, forwardingunit_1_rw_maf, forwardingunit_1_rw_ofop1, forwardingunit_1_rw_ofop2,
       isWriteBack, ldusestall, not_1_out, not_2_out, not_3_out;
  wire [1:0] forwardingunit_1_rw_exop1, forwardingunit_1_rw_exop2;
  wire [3:0] Addr, Control_2_q_2, cu_1_alusignals;
  wire [12:0] Control_2_q, Control_q, cu_1_iswb, multiplexer_2_out;
  wire [12:1] Control_3_q;
  wire [23:0] exu_1_branchtargetout, if_1_pc, PC_2_q, PC_3_q, PC_4_q, PC_q;
  wire [31:0] A_q, aluResult_2_q, aluResult_q, B_q, BranchTarget_q, Data, DispVal, exu_1_aluresult,
       if_1_instruction, instruction_2_q, instruction_3_q, Instruction_q, ldResult_q, ma_1_ldresult,
       multiplexer_1_out, multiplexer_3_out, multiplexer_4_out, multiplexer_5_out, multiplexer_6_out,
       multiplexer_7_out, of_1_a, of_1_b, of_1_branchtarget, of_1_op2, op2_2_q, op2_q;

  Clock clock_1 (.out(clk));
  IF if_1 (
    .isBranchTaken(bls), .Instruction(if_1_instruction), .branchTarget(exu_1_branchtargetout),
    .IFstageclock(and_1_out), .PC(if_1_pc));  // open: reset
  and and_1 (and_1_out, clk, not_1_out);
  not not_1 (not_1_out, ldusestall);
  not not_2 (not_2_out, bls);
  Multiplexer #(.width(32)) multiplexer_1 (
    .in0(32'h68000000), .in1(if_1_instruction), .out(multiplexer_1_out), .sel(not_2_out));  // open: en
  Hex_Digit_Display hex_digit_display_1 (.value(DispVal[31:28]));  // open: dp
  Register #(.width(32), .trigger("falling")) INSTR (
    .D(multiplexer_1_out), .Q(out_2), .clk(and_1_out));  // open: en, clr
  Register #(.width(24), .trigger("falling")) PC (.D(if_1_pc), .Q(PC_q), .clk(and_1_out));  // open: en, clr
  Hex_Digit_Display hex_digit_display_2 (.value(DispVal[27:24]));  // open: dp
  Hex_Digit_Display hex_digit_display_3 (.value(DispVal[23:20]));  // open: dp
  Hex_Digit_Display hex_digit_display_4 (.value(DispVal[15:12]));  // open: dp
  Hex_Digit_Display hex_digit_display_5 (.value(DispVal[19:16]));  // open: dp
  CU cu_1 (
    .isWb(cu_1_iswb[0]), .isUbranch(cu_1_iswb[1]), .isImmediate(cu_1_iswb[2]), .isLd(cu_1_iswb[7]),
    .isSt(cu_1_iswb[12]), .isBeq(cu_1_iswb[8]), .isBgt(cu_1_iswb[11]), .isCall(cu_1_iswb[10]),
    .isRet(cu_1_iswb[9]), .ALUSignals(cu_1_alusignals), .Instruction(out_2));
  OF of_1 (
    .Instruction(out_2), .PC(PC_q), .branchTarget(of_1_branchtarget), .isSt(cu_1_iswb[12]),
    .isImmx(cu_1_iswb[2]), .A(of_1_a), .B(of_1_b), .op2(of_1_op2), .isRet(cu_1_iswb[9]), .writeData(Data),
    .writeAddress(Addr), .isWb(isWriteBack), .clock(clk), .displayAddress(in_1), .displayOut(DispVal),
    .isCall(cu_1_iswb[10]), .data(Data), .PinOP2(forwardingunit_1_rw_ofop2),
    .PinOP1(forwardingunit_1_rw_ofop1));
  Hex_Digit_Display hex_digit_display_6 (.value(DispVal[7:4]));  // open: dp
  Hex_Digit_Display hex_digit_display_7 (.value(DispVal[11:8]));  // open: dp
  Hex_Digit_Display hex_digit_display_8 (.value(DispVal[3:0]));  // open: dp
  Multiplexer #(.width(13)) multiplexer_2 (
    .in0({13{1'b0}}), .in1({cu_1_iswb[12:7], cu_1_alusignals, cu_1_iswb[2:0]}), .out(multiplexer_2_out),
    .sel(not_3_out));  // open: en
  not not_3 (not_3_out, bls);
  Multiplexer #(.width(32)) multiplexer_3 (
    .in0(32'h68000000), .in1(out_2), .out(multiplexer_3_out), .sel(not_3_out));  // open: en
  Register #(.width(13), .trigger("falling")) Control (
    .D(multiplexer_2_out), .Q(Control_q), .clk(clk));  // open: en, clr
  Register #(.width(32), .trigger("falling")) Instruction (
    .D(multiplexer_3_out), .Q(Instruction_q), .clk(clk));  // open: en, clr
  Register #(.width(32), .trigger("falling")) op2 (.D(of_1_op2), .Q(op2_q), .clk(clk));  // open: en, clr
  Register #(.width(32), .trigger("falling")) A (.D(of_1_a), .Q(A_q), .clk(clk));  // open: en, clr
  Register #(.width(32), .trigger("falling")) B (.D(of_1_b), .Q(B_q), .clk(clk));  // open: en, clr
  Register #(.width(32), .trigger("falling")) BranchTarget (
    .D(of_1_branchtarget), .Q(BranchTarget_q), .clk(clk));  // open: en, clr
  Register #(.width(24), .trigger("falling")) PC_2 (.D(PC_q), .Q(PC_2_q), .clk(clk));  // open: en, clr
  loadUseDetect loadusedetect_1 (.IFOF(out_2), .OFEX(Instruction_q), .Stall(ldusestall));
  Multiplexer #(.width(32)) multiplexer_4 (.in0(Data), .in1(op2_q), .out(multiplexer_4_out));  // open: sel, en
  Multiplexer #(.select(2), .width(32)) multiplexer_5 (
    .in0(A_q), .in1(Data), .in2(aluResult_q), .in3(aluResult_q), .out(multiplexer_5_out),
    .sel(forwardingunit_1_rw_exop1));  // open: en
  Multiplexer #(.select(2), .width(32)) multiplexer_6 (
    .in0(B_q), .in1(Data), .in2(aluResult_q), .in3(aluResult_q), .out(multiplexer_6_out),
    .sel(forwardingunit_1_rw_exop2));  // open: en
  EXU exu_1 (
    .isBeq(Control_q[8]), .isUbranch(Control_q[1]), .isBgt(Control_q[11]), .branchTargetIn(BranchTarget_q),
    .A(multiplexer_5_out), .aluSignals(Control_q[6:3]), .B(multiplexer_6_out), .Clock(clk),
    .isBranchTaken(bls), .branchTargetOut(exu_1_branchtargetout), .ALUResult(exu_1_aluresult),
    .isRet(Control_q[9]));
  ForwardingUnit forwardingunit_1 (
    .IFOF(out_2), .OFEX(Instruction_q), .EXMA(instruction_2_q), .MARW(instruction_3_q),
    .MA_EXOP2(forwardingunit_1_rw_exop2[1]), .MA_EXOP1(forwardingunit_1_rw_exop1[1]),
    .RW_OFOP2(forwardingunit_1_rw_ofop2), .RW_OFOP1(forwardingunit_1_rw_ofop1),
    .RW_EXOP2(forwardingunit_1_rw_exop2[0]), .RW_EXOP1(forwardingunit_1_rw_exop1[0]),
    .RW_MAF(forwardingunit_1_rw_maf));
  Register #(.width(13), .trigger("falling")) Control_2 (
    .D(Control_q), .Q({Control_2_q[12:7], Control_2_q_2, Control_2_q[2:0]}), .clk(clk));  // open: en, clr
  Register #(.width(32), .trigger("falling")) instruction_2 (
    .D(Instruction_q), .Q(instruction_2_q), .clk(clk));  // open: en, clr
  Register #(.width(32), .trigger("falling")) op2_2 (.D(multiplexer_4_out), .Q(op2_2_q), .clk(clk));  // open: en, clr
  Register #(.width(32), .trigger("falling")) aluResult (
    .D(exu_1_aluresult), .Q(aluResult_q), .clk(clk));  // open: en, clr
  Register #(.width(24), .trigger("falling")) PC_3 (.D(PC_2_q), .Q(PC_3_q), .clk(clk));  // open: en, clr
  Multiplexer #(.width(32)) multiplexer_7 (
    .in0(Data), .in1(op2_2_q), .out(multiplexer_7_out), .sel(forwardingunit_1_rw_maf));  // open: en
  MA ma_1 (
    .ldResult(ma_1_ldresult), .op2(multiplexer_7_out), .isLd(Control_2_q[7]), .isSt(Control_2_q[12]),
    .ALUResult(aluResult_q), .Clock(clk));
  Register #(.width(13), .trigger("falling")) Control_3 (
    .D({Control_2_q[12:7], Control_2_q_2, Control_2_q[2:0]}), .Q({Control_3_q, isWriteBack}), .clk(clk));  // open: en, clr
  Register #(.width(32), .trigger("falling")) instruction_3 (
    .D(instruction_2_q), .Q(instruction_3_q), .clk(clk));  // open: en, clr
  Register #(.width(32), .trigger("falling")) aluResult_2 (
    .D(aluResult_q), .Q(aluResult_2_q), .clk(clk));  // open: en, clr
  Register #(.width(32), .trigger("falling")) ldResult (.D(ma_1_ldresult), .Q(ldResult_q), .clk(clk));  // open: en, clr
  Register #(.width(24), .trigger("falling")) PC_4 (.D(PC_3_q), .Q(PC_4_q), .clk(clk));  // open: en, clr
  RW rw_1 (
    .Instruction(instruction_3_q), .ldResult(ldResult_q), .isLd(Control_3_q[7]), .ALUResult(aluResult_2_q),
    .isCall(Control_3_q[10]), .PC(PC_4_q), .Address(Addr), .storeData(Data));

  // Other names for the same wires on the sheet: nDispReg[3:0] = in_1
endmodule
